# Fritzing sketch WemosD1MiniTemp (saved by Fritzing 0.9.6b)

parts:
  WeMos_D1_Mini1 = WeMos D1 Mini
  DS1 = DS18B20 1-Wire Temperature Sensor [part_number=DS18B20]

nets:
  3V3: WeMos_D1_Mini1.3V3, DS1.VDD
  N1: WeMos_D1_Mini1.D4, DS1.DQ
  N2: WeMos_D1_Mini1.G, DS1.GND
